// Logisim project tp34-template.circ as structural Verilog: 2 circuits, main circuit TP34
module TP34 (
);

  wire disp0i_a_out, disp0i_b_out, disp0i_c_out, disp0i_d_out, disp0i_e_out, disp0i_f_out, disp0i_g_out,
       disp0i_p_out, disp1i_a_out, disp1i_b_out, disp1i_c_out, disp1i_d_out, disp1i_e_out, disp1i_f_out,
       disp1i_g_out, disp1i_p_out, disp2i_a_out, disp2i_b_out, disp2i_c_out, disp2i_d_out, disp2i_e_out,
       disp2i_f_out, disp2i_g_out, disp2i_p_out;
  wire [2:0] undriven, undriven_2, undriven_3;

  Button But ();  // open: out
  Clock clk ();  // open: out
  Button reset ();  // open: out
  disp_interface disp2i (
    .a_out(disp2i_a_out), .b_out(disp2i_b_out), .c_out(disp2i_c_out), .d_out(disp2i_d_out),
    .e_out(disp2i_e_out), .f_out(disp2i_f_out), .g_out(disp2i_g_out), .p_out(disp2i_p_out));  // open: a_in, b_in, c_in, d_in, e_in, f_in, g_in, p_in
  disp_interface disp1i (
    .a_out(disp1i_a_out), .b_out(disp1i_b_out), .c_out(disp1i_c_out), .d_out(disp1i_d_out),
    .e_out(disp1i_e_out), .f_out(disp1i_f_out), .g_out(disp1i_g_out), .p_out(disp1i_p_out));  // open: a_in, b_in, c_in, d_in, e_in, f_in, g_in, p_in
  disp_interface disp0i (
    .a_out(disp0i_a_out), .b_out(disp0i_b_out), .c_out(disp0i_c_out), .d_out(disp0i_d_out),
    .e_out(disp0i_e_out), .f_out(disp0i_f_out), .g_out(disp0i_g_out), .p_out(disp0i_p_out));  // open: a_in, b_in, c_in, d_in, e_in, f_in, g_in, p_in
  _7_Segment_Display Disp2 (
    .g(disp2i_g_out), .f(disp2i_f_out), .a(disp2i_a_out), .b(disp2i_b_out), .e(disp2i_e_out),
    .d(disp2i_d_out), .c(disp2i_c_out), .dp(disp2i_p_out));
  _7_Segment_Display Disp1 (
    .g(disp1i_g_out), .f(disp1i_f_out), .a(disp1i_a_out), .b(disp1i_b_out), .e(disp1i_e_out),
    .d(disp1i_d_out), .c(disp1i_c_out), .dp(disp1i_p_out));
  _7_Segment_Display Disp0 (
    .g(disp0i_g_out), .f(disp0i_f_out), .a(disp0i_a_out), .b(disp0i_b_out), .e(disp0i_e_out),
    .d(disp0i_d_out), .c(disp0i_c_out), .dp(disp0i_p_out));
  LED Q22 (.in(undriven[2]));
  LED Q12 (.in(undriven_2[2]));
  LED Q02 (.in(undriven_3[2]));
  LED Q21 (.in(undriven[1]));
  LED Q11 (.in(undriven_2[1]));
  LED Q01 (.in(undriven_3[1]));
  LED Q20 (.in(undriven[0]));
  LED Q10 (.in(undriven_2[0]));
  LED Q00 (.in(undriven_3[0]));
endmodule

module disp_interface (
  input  a_in,
  input  b_in,
  input  c_in,
  input  d_in,
  input  e_in,
  input  f_in,
  input  g_in,
  input  p_in,
  output a_out,
  output b_out,
  output c_out,
  output d_out,
  output e_out,
  output f_out,
  output g_out,
  output p_out
);

  not not_1 (a_out, a_in);
  not not_2 (b_out, b_in);
  not not_3 (c_out, c_in);
  not not_4 (d_out, d_in);
  not not_5 (e_out, e_in);
  not not_6 (f_out, f_in);
  not not_7 (g_out, g_in);
  not not_8 (p_out, p_in);
endmodule
